// Logisim project ALS.circ as structural Verilog: 5 circuits, main circuit main
module main (
  input  [3:0] A,
  input  [3:0] B,
  input  [3:0] Instruction,
  output [3:0] ANS
);

  wire [3:0] arithmetic_1_ans, logical_1_ans, propagation_1_ans, shift_1_ans;

  Arithmetic arithmetic_1 (.A(A), .B(B), .Selection(Instruction[1:0]), .Ans(arithmetic_1_ans));
  Logical logical_1 (.A(A), .B(B), .Selection(Instruction[1:0]), .Ans(logical_1_ans));
  Shift shift_1 (.A(A), .Selection(Instruction[1:0]), .Ans(shift_1_ans));
  Propagation propagation_1 (.A(A), .B(B), .Selection(Instruction[1:0]), .Ans(propagation_1_ans));
  Multiplexer #(.select(2), .width(4)) multiplexer_1 (
    .in0(arithmetic_1_ans), .in1(logical_1_ans), .in2(shift_1_ans), .in3(propagation_1_ans), .out(ANS),
    .sel(Instruction[3:2]));  // open: en

  // Notes on the sheet:
  //   Arithmetic
  //   Logical
  //   Shift
  //   Propagation
endmodule

module Arithmetic (
  input  [3:0] A,
  input  [3:0] B,
  input  [1:0] Selection,
  output [3:0] Ans
);

  wire [3:0] multiplexer_1_out, negator_1_out;

  Negator #(.width(4)) negator_1 (.in(B), .out(negator_1_out));
  Multiplexer #(.select(2), .width(4)) multiplexer_1 (
    .in0(B), .in1(negator_1_out), .in2(4'b0001), .in3(4'b1111), .out(multiplexer_1_out), .sel(Selection));  // open: en
  Adder #(.width(4)) adder_1 (.a(A), .b(multiplexer_1_out), .out(Ans), .cin(1'b0));  // open: cout
endmodule

module Logical (
  input  [3:0] A,
  input  [3:0] B,
  input  [1:0] Selection,
  output [3:0] Ans
);

  wire [3:0] and_1_out, or_1_out, xnor_1_out, xor_1_out;

  assign and_1_out = B & A;  // AND_Gate and_1, 4 bits wide
  assign or_1_out = A | B;  // OR_Gate or_1, 4 bits wide
  assign xor_1_out = A ^ B;  // XOR_Gate xor_1, 4 bits wide
  assign xnor_1_out = ~(A ^ B);  // XNOR_Gate xnor_1, 4 bits wide
  Multiplexer #(.select(2), .width(4)) multiplexer_1 (
    .in0(and_1_out), .in1(or_1_out), .in2(xor_1_out), .in3(xnor_1_out), .out(Ans), .sel(Selection));  // open: en
endmodule

module Shift (
  input  [3:0] A,
  input  [1:0] Selection,
  output [3:0] Ans
);

  wire [3:0] shifter_1_out, shifter_2_out, shifter_3_out, shifter_4_out;

  Shifter #(.width(4)) shifter_1 (.in(A), .\dist (2'b01), .out(shifter_1_out));
  Shifter #(.width(4), .shift("ar")) shifter_2 (.in(A), .\dist (2'b01), .out(shifter_2_out));
  Shifter #(.width(4), .shift("rl")) shifter_3 (.in(A), .\dist (2'b01), .out(shifter_3_out));
  Shifter #(.width(4), .shift("rr")) shifter_4 (.in(A), .\dist (2'b01), .out(shifter_4_out));
  Multiplexer #(.select(2), .width(4)) multiplexer_1 (
    .in0(shifter_1_out), .in1(shifter_2_out), .in2(shifter_3_out), .in3(shifter_4_out), .out(Ans),
    .sel(Selection));  // open: en
endmodule

module Propagation (
  input  [3:0] A,
  input  [3:0] B,
  input  [1:0] Selection,
  output [3:0] Ans
);

  wire [3:0] not_1_out, not_2_out;

  assign not_1_out = ~A;  // NOT_Gate not_1, 4 bits wide
  assign not_2_out = ~B;  // NOT_Gate not_2, 4 bits wide
  Multiplexer #(.select(2), .width(4)) multiplexer_1 (
    .in0(A), .in1(B), .in2(not_1_out), .in3(not_2_out), .out(Ans), .sel(Selection));  // open: en
endmodule
