// Logisim project BoothsAlgorithm.circ as structural Verilog: 1 circuit, main circuit main
module main (
);

  wire and_1_out, clock_1_out, not_1_out, SC_carry;
  wire [0:0] Q_n_1_q;
  wire [3:0] A_q, adder_1_out, B_q, Q_q, subtractor_1_out;
  wire [7:0] multiplexer_1_out, shifter_1_out;

  Register #(.width(4)) A (.D(shifter_1_out[7:4]), .Q(A_q), .clk(and_1_out));  // open: en, clr
  Register #(.width(4)) B (.Q(B_q), .clk(and_1_out));  // open: D, en, clr
  Register #(.width(4)) Q (.D(shifter_1_out[3:0]), .Q(Q_q), .clk(and_1_out));  // open: en, clr
  Adder #(.width(4)) adder_1 (.a(A_q), .b(B_q), .out(adder_1_out), .cin(1'b0));  // open: cout
  Subtractor #(.width(4)) subtractor_1 (.a(A_q), .b(B_q), .out(subtractor_1_out), .bin(1'b0));  // open: bout
  Register #(.width(1)) Q_n_1 (.D(Q_q[0]), .Q(Q_n_1_q[0]), .clk(and_1_out));  // open: en, clr
  and and_1 (and_1_out, clock_1_out, not_1_out);
  Clock clock_1 (.out(clock_1_out));
  Counter #(.width(3), .max('h4), .ongoal("stay")) SC (
    .carry(SC_carry), .clk(clock_1_out));  // open: load, D, count, Q, clr
  not not_1 (not_1_out, SC_carry);
  Multiplexer #(.select(2), .width(8), .enable("false")) multiplexer_1 (
    .in0({A_q, Q_q}), .in1({adder_1_out, Q_q}), .in2({subtractor_1_out, Q_q}), .in3({A_q, Q_q}),
    .out(multiplexer_1_out), .sel({Q_q[0], Q_n_1_q[0]}));
  Shifter #(.shift("ar")) shifter_1 (.in(multiplexer_1_out), .\dist (3'b001), .out(shifter_1_out));
endmodule
