// Logisim project Bus-system.circ as structural Verilog
module Parallel_Bus_System (
  input  [1:0] in_1,
  input  [1:0] in_2
);

  wire clock_1_out, decoder_1_out0, decoder_1_out1, decoder_1_out2, decoder_1_out3;
  wire [3:0] A_q, B_q, C_q, D_q, multiplexer_1_out;

  Decoder #(.select(2)) decoder_1 (
    .out0(decoder_1_out0), .out1(decoder_1_out1), .out2(decoder_1_out2), .out3(decoder_1_out3), .sel(in_1));  // open: en
  Clock clock_1 (.out(clock_1_out));
  Register #(.width(4)) A (.D(multiplexer_1_out), .en(decoder_1_out0), .Q(A_q), .clk(clock_1_out));  // open: clr
  Register #(.width(4)) B (.D(multiplexer_1_out), .en(decoder_1_out1), .Q(B_q), .clk(clock_1_out));  // open: clr
  Register #(.width(4)) C (.D(multiplexer_1_out), .en(decoder_1_out2), .Q(C_q), .clk(clock_1_out));  // open: clr
  Register #(.width(4)) D (.D(multiplexer_1_out), .en(decoder_1_out3), .Q(D_q), .clk(clock_1_out));  // open: clr
  Multiplexer #(.select(2), .width(4)) multiplexer_1 (
    .in0(A_q), .in1(B_q), .in2(C_q), .in3(D_q), .out(multiplexer_1_out), .sel(in_2));  // open: en
endmodule

module Serial_Bus_System (
  input  [1:0] in_1,
  input  [1:0] in_2
);

  wire A_out, and_1_out, B_out, C_out, clock_1_out, controlled_buffer_1_out, counter_1_carry, D_out,
       decoder_1_out0, decoder_1_out1, decoder_1_out2, decoder_1_out3, decoder_2_out0, decoder_2_out1,
       decoder_2_out2, decoder_2_out3, not_1_out, or_1_out, or_2_out, or_3_out, or_4_out;

  Counter #(.width(3), .max('h4), .ongoal("stay")) counter_1 (
    .carry(counter_1_carry), .clk(clock_1_out));  // open: load, D, count, Q, clr
  not not_1 (not_1_out, counter_1_carry);
  Decoder #(.select(2)) decoder_1 (
    .out0(decoder_1_out0), .out1(decoder_1_out1), .out2(decoder_1_out2), .out3(decoder_1_out3), .sel(in_1));  // open: en
  and and_1 (and_1_out, not_1_out, clock_1_out);
  Clock clock_1 (.out(clock_1_out));
  or or_1 (or_1_out, decoder_1_out0, decoder_2_out0);
  or or_2 (or_2_out, decoder_1_out1, decoder_2_out1);
  or or_3 (or_3_out, decoder_1_out2, decoder_2_out2);
  or or_4 (or_4_out, decoder_1_out3, decoder_2_out3);
  Shift_Register #(.length(4)) A (
    .shift(or_1_out), .in(controlled_buffer_1_out), .clk(and_1_out), .out(A_out));  // open: load, clr, d0, q0, d1, q1, d2, q2, d3, q3
  Shift_Register #(.length(4)) B (
    .shift(or_2_out), .in(controlled_buffer_1_out), .clk(and_1_out), .out(B_out));  // open: load, clr, d0, q0, d1, q1, d2, q2, d3, q3
  Shift_Register #(.length(4)) C (
    .shift(or_3_out), .in(controlled_buffer_1_out), .clk(and_1_out), .out(C_out));  // open: load, clr, d0, q0, d1, q1, d2, q2, d3, q3
  Shift_Register #(.length(4)) D (
    .shift(or_4_out), .in(controlled_buffer_1_out), .clk(and_1_out), .out(D_out));  // open: load, clr, d0, q0, d1, q1, d2, q2, d3, q3
  Decoder #(.select(2)) decoder_2 (
    .out0(decoder_2_out0), .out1(decoder_2_out1), .out2(decoder_2_out2), .out3(decoder_2_out3), .sel(in_2));  // open: en
  assign controlled_buffer_1_out = decoder_2_out0 ? A_out : 1'bz;  // Controlled_Buffer controlled_buffer_1
  assign controlled_buffer_1_out = decoder_2_out1 ? B_out : 1'bz;  // Controlled_Buffer controlled_buffer_2
  assign controlled_buffer_1_out = decoder_2_out2 ? C_out : 1'bz;  // Controlled_Buffer controlled_buffer_3
  assign controlled_buffer_1_out = decoder_2_out3 ? D_out : 1'bz;  // Controlled_Buffer controlled_buffer_4
endmodule
