// Logisim project Cache.circ as structural Verilog: 3 circuits, main circuit main
module main (
  input  [7:0] D,
  input  [7:0] A,
  input  [7:0] D_2
);

  wire [15:0] B1_q, B2_q, B3_q, B4_q;

  Register #(.width(16)) B1 (.Q(B1_q));  // open: D, en, clk, clr
  Register #(.width(16)) B2 (.Q(B2_q));  // open: D, en, clk, clr
  Register #(.width(16)) B3 (.Q(B3_q));  // open: D, en, clk, clr
  Register #(.width(16)) B4 (.Q(B4_q));  // open: D, en, clk, clr
  // XNOR_Gate xnor_1 has open pins: in0=D, in1=B1_q[15:8], out=open
  // XNOR_Gate xnor_2 has open pins: in0=D, in1=B2_q[15:8], out=open
  // XNOR_Gate xnor_3 has open pins: in0=D, in1=B3_q[15:8], out=open
  // XNOR_Gate xnor_4 has open pins: in0=D, in1=B4_q[15:8], out=open
  RAM #(.dataWidth(16)) ram_1 ();  // open: addr, data, sel, clk, ld, clr
endmodule

module Matcher (
  input  [7:0] D,
  input  [7:0] M,
  input  [7:0] X,
  output O
);

  wire [7:0] and_1_out, and_2_out, xnor_1_out;

  assign and_1_out = D & M;  // AND_Gate and_1, 8 bits wide
  assign and_2_out = M & X;  // AND_Gate and_2, 8 bits wide
  assign xnor_1_out = ~(and_1_out ^ and_2_out);  // XNOR_Gate xnor_1, 8 bits wide
  and and_3 (O, xnor_1_out[0], xnor_1_out[1], xnor_1_out[2], xnor_1_out[3], xnor_1_out[4], xnor_1_out[5], xnor_1_out[6], xnor_1_out[7]);
endmodule

module read (
  output [7:0] out_1
);

  wire clock_1_out, matcher_1_o, matcher_2_o, matcher_3_o, matcher_4_o, not_1_out, shift_register_1_q0,
       shift_register_1_q1, shift_register_1_q2, shift_register_1_q3;
  wire [1:0] priority_encoder_1_out;
  wire [7:0] D_q, M_q, X1_q, X2_q, X3_q, X4_q;

  Register D (.Q(D_q));  // open: D, en, clk, clr
  Register M (.Q(M_q));  // open: D, en, clk, clr
  Register X1 (.Q(X1_q));  // open: D, en, clk, clr
  Register X2 (.Q(X2_q));  // open: D, en, clk, clr
  Register X3 (.Q(X3_q));  // open: D, en, clk, clr
  Register X4 (.Q(X4_q));  // open: D, en, clk, clr
  Matcher matcher_1 (.D(D_q), .M(M_q), .X(X1_q), .O(matcher_1_o));
  Matcher matcher_2 (.D(D_q), .M(M_q), .X(X2_q), .O(matcher_2_o));
  Matcher matcher_3 (.D(D_q), .M(M_q), .X(X3_q), .O(matcher_3_o));
  Matcher matcher_4 (.D(D_q), .M(M_q), .X(X4_q), .O(matcher_4_o));
  not not_1 (not_1_out, 1'b1);
  Clock clock_1 (.out(clock_1_out));
  Shift_Register #(.length(4)) shift_register_1 (
    .shift(not_1_out), .clk(clock_1_out), .load(1'b1), .d0(matcher_1_o), .q0(shift_register_1_q0),
    .d1(matcher_2_o), .q1(shift_register_1_q1), .d2(matcher_3_o), .q2(shift_register_1_q2), .d3(matcher_4_o),
    .q3(shift_register_1_q3));  // open: in, out, clr
  Priority_Encoder #(.select(2)) priority_encoder_1 (
    .in0(shift_register_1_q3), .in1(shift_register_1_q2), .in2(shift_register_1_q1),
    .in3(shift_register_1_q0), .out(priority_encoder_1_out));  // open: gs, en_out, en_in
  Multiplexer #(.select(2), .width(8)) multiplexer_1 (
    .in0(X4_q), .in1(X3_q), .in2(X2_q), .in3(X1_q), .out(out_1), .sel(priority_encoder_1_out));  // open: en
endmodule
