// Logisim project Excess-3.circ as structural Verilog: 1 circuit, main circuit main
module main (
  input  [3:0] in_1,
  input  [3:0] in_2,
  input  [3:0] in_3,
  input  [3:0] in_4,
  input  [3:0] in_5,
  input  [3:0] in_6
);

  wire adder_1_cout;
  wire [3:0] adder_1_out, adder_2_out, multiplexer_1_out, multiplexer_2_out;

  Adder #(.width(4)) adder_1 (.a(in_1), .b(in_2), .out(adder_1_out), .cin(1'b0), .cout(adder_1_cout));
  Multiplexer #(.width(4), .enable("false")) multiplexer_1 (
    .in0(in_3), .in1(in_4), .out(multiplexer_1_out), .sel(adder_1_cout));
  Adder #(.width(4)) adder_2 (.a(adder_1_out), .b(multiplexer_1_out), .out(adder_2_out), .cin(1'b0));  // open: cout
  Multiplexer #(.width(4), .enable("false")) multiplexer_2 (
    .in0(in_5), .in1(in_6), .out(multiplexer_2_out), .sel(adder_1_cout));
  // Probe on multiplexer_2_out
  // Probe on adder_2_out
endmodule
