// Logisim project Instruction-Cycle.circ as structural Verilog: 6 circuits, main circuit main
module main (
  input  FGI
);

  wire and_1_out, and_2_out, and_3_out, bitselector_1_out, clock_1_out, decoder_1_out0, decoder_1_out1,
       decoder_1_out2, decoder_1_out4, decoder_1_out5, decoder_2_out1, decoder_2_out4, decoder_2_out7,
       or_1_out, or_2_out, or_3_out;
  wire [2:0] priority_encoder_1_out;
  wire [2:2] ALS;
  wire [3:0] counter_1_q;
  wire [11:0] AR_q, bit_extender_1_out, bit_extender_2_out, PC_q;
  wire [15:0] AC_q, als_1_ans, bit_extender_3_out, bit_extender_4_out, DR_q, IR_q, multiplexer_1_out,
       ram_1_data;

  Counter #(.width(4), .max('hf)) counter_1 (.Q(counter_1_q), .clk(clock_1_out));  // open: load, D, count, carry, clr
  Decoder #(.select(4)) decoder_1 (
    .out0(decoder_1_out0), .out1(decoder_1_out1), .out2(decoder_1_out2), .out4(decoder_1_out4),
    .out5(decoder_1_out5), .sel(counter_1_q));  // open: out3, out6, out7, out8, out9, out10, out11, out12, out13, out14, out15, en
  or or_1 (or_1_out, decoder_1_out0, decoder_1_out2);
  or or_2 (or_2_out, decoder_1_out1, and_2_out);
  or or_3 (or_3_out, decoder_1_out1, and_1_out);
  and and_1 (and_1_out, decoder_1_out4, ALS[2], decoder_2_out1);
  Bit_Extender #(.in_width(16), .out_width(12)) bit_extender_1 (.in(multiplexer_1_out), .out(bit_extender_1_out));
  Bit_Extender #(.in_width(16), .out_width(12)) bit_extender_2 (.in(multiplexer_1_out), .out(bit_extender_2_out));
  ALS als_1 (.Instruction({1'b0, ALS[2], 2'b00}), .A(AC_q), .B(DR_q), .ANS(als_1_ans));
  Clock clock_1 (.out(clock_1_out));
  RAM #(.addrWidth(12), .dataWidth(16)) ram_1 (
    .addr(AR_q), .data(ram_1_data), .clk(clock_1_out));  // open: sel, ld, clr
  Register #(.width(12)) AR (.D(bit_extender_1_out), .en(or_1_out), .Q(AR_q), .clk(clock_1_out));  // open: clr
  Counter #(.width(12), .max('hfff)) PC (
    .load(and_3_out), .D(bit_extender_2_out), .count(or_2_out), .Q(PC_q), .clk(clock_1_out));  // open: carry, clr
  Register #(.width(16)) DR (.D(multiplexer_1_out), .en(decoder_1_out4), .Q(DR_q), .clk(clock_1_out));  // open: clr
  Register #(.width(16)) AC (.D(als_1_ans), .en(decoder_1_out5), .Q(AC_q), .clk(clock_1_out));  // open: clr
  Register #(.width(16)) IR (.D(multiplexer_1_out), .en(decoder_1_out1), .Q(IR_q), .clk(clock_1_out));  // open: clr
  assign bit_extender_3_out = {{4{1'b0}}, AR_q};  // Bit_Extender bit_extender_3
  assign bit_extender_4_out = {{4{1'b0}}, PC_q};  // Bit_Extender bit_extender_4
  Priority_Encoder priority_encoder_1 (
    .in1(and_3_out), .in2(decoder_1_out0), .in5(decoder_1_out2), .in7(or_3_out), .out(priority_encoder_1_out));  // open: in0, in3, in4, in6, en_in, gs, en_out
  and and_2 (and_2_out, decoder_2_out7, bitselector_1_out, IR_q[9], FGI);
  Multiplexer #(.select(3), .width(16)) multiplexer_1 (
    .in1(bit_extender_3_out), .in2(bit_extender_4_out), .in3(DR_q), .in5(IR_q), .in7(ram_1_data),
    .out(multiplexer_1_out), .sel(priority_encoder_1_out));  // open: in0, in4, in6, en
  Decoder #(.select(3)) decoder_2 (
    .out0(ALS[2]), .out1(decoder_2_out1), .out4(decoder_2_out4), .out7(decoder_2_out7), .sel(IR_q[14:12]));  // open: out2, out3, out5, out6, en
  BitSelector #(.width(16)) bitselector_1 (.in(IR_q), .out(bitselector_1_out), .sel(4'b1111));
  and and_3 (and_3_out, decoder_2_out4, decoder_1_out4);
  // Probe on bitselector_1_out
endmodule

module Arithmetic (
  input  [15:0] A,
  input  [15:0] B,
  input  [1:0] Selection,
  output [15:0] Ans
);

  wire [15:0] multiplexer_1_out, negator_1_out;

  Negator #(.width(16)) negator_1 (.in(B), .out(negator_1_out));
  Multiplexer #(.select(2), .width(16)) multiplexer_1 (
    .in0(B), .in1(negator_1_out), .in2(16'h1), .in3({16{1'b1}}), .out(multiplexer_1_out), .sel(Selection));  // open: en
  Adder #(.width(16)) adder_1 (.a(A), .b(multiplexer_1_out), .out(Ans), .cin(1'b0));  // open: cout
endmodule

module Logical (
  input  [15:0] A,
  input  [15:0] B,
  input  [1:0] Selection,
  output [15:0] Ans
);

  wire [15:0] and_1_out, or_1_out, xnor_1_out, xor_1_out;

  assign and_1_out = B & A;  // AND_Gate and_1, 16 bits wide
  assign or_1_out = A | B;  // OR_Gate or_1, 16 bits wide
  assign xor_1_out = A ^ B;  // XOR_Gate xor_1, 16 bits wide
  assign xnor_1_out = ~(A ^ B);  // XNOR_Gate xnor_1, 16 bits wide
  Multiplexer #(.select(2), .width(16)) multiplexer_1 (
    .in0(and_1_out), .in1(or_1_out), .in2(xor_1_out), .in3(xnor_1_out), .out(Ans), .sel(Selection));  // open: en
endmodule

module Shift (
  input  [15:0] A,
  input  [1:0] Selection,
  output [15:0] Ans
);

  wire [15:0] shifter_1_out, shifter_2_out, shifter_3_out, shifter_4_out;

  Shifter #(.width(16)) shifter_1 (.in(A), .\dist (4'b0001), .out(shifter_1_out));
  Shifter #(.width(16), .shift("ar")) shifter_2 (.in(A), .\dist (4'b0001), .out(shifter_2_out));
  Shifter #(.width(16), .shift("rl")) shifter_3 (.in(A), .\dist (4'b0001), .out(shifter_3_out));
  Shifter #(.width(16), .shift("rr")) shifter_4 (.in(A), .\dist (4'b0001), .out(shifter_4_out));
  Multiplexer #(.select(2), .width(16)) multiplexer_1 (
    .in0(shifter_1_out), .in1(shifter_2_out), .in2(shifter_3_out), .in3(shifter_4_out), .out(Ans),
    .sel(Selection));  // open: en
endmodule

module Propagation (
  input  [15:0] A,
  input  [15:0] B,
  input  [1:0] Selection,
  output [15:0] Ans
);

  wire [15:0] not_1_out, not_2_out;

  assign not_1_out = ~A;  // NOT_Gate not_1, 16 bits wide
  assign not_2_out = ~B;  // NOT_Gate not_2, 16 bits wide
  Multiplexer #(.select(2), .width(16)) multiplexer_1 (
    .in0(A), .in1(B), .in2(not_1_out), .in3(not_2_out), .out(Ans), .sel(Selection));  // open: en
endmodule

module ALS (
  input  [15:0] A,
  input  [15:0] B,
  input  [3:0] Instruction,
  output [15:0] ANS
);

  wire [15:0] arithmetic_1_ans, logical_1_ans, propagation_1_ans, shift_1_ans;

  Arithmetic arithmetic_1 (.A(A), .B(B), .Selection(Instruction[1:0]), .Ans(arithmetic_1_ans));
  Logical logical_1 (.A(A), .B(B), .Selection(Instruction[1:0]), .Ans(logical_1_ans));
  Shift shift_1 (.A(A), .Selection(Instruction[1:0]), .Ans(shift_1_ans));
  Propagation propagation_1 (.A(A), .B(B), .Selection(Instruction[1:0]), .Ans(propagation_1_ans));
  Multiplexer #(.select(2), .width(16)) multiplexer_1 (
    .in0(arithmetic_1_ans), .in1(logical_1_ans), .in2(shift_1_ans), .in3(propagation_1_ans), .out(ANS),
    .sel(Instruction[3:2]));  // open: en

  // Notes on the sheet:
  //   Arithmetic
  //   Logical
  //   Shift
  //   Propagation
endmodule
