// Logisim project Multiplication.circ as structural Verilog: 1 circuit, main circuit main
module main (
  input  Qs,
  input  Bs
);

  wire and_1_out, clock_1_out, not_1_out, SC_carry, xor_1_out;
  wire [3:0] A_q, adder_1_out, B_q, Q_q;
  wire [8:0] multiplexer_1_out, shifter_1_out;
  wire [8:8] adder_1_cout, E_q;

  Register #(.width(4)) A (.D(shifter_1_out[7:4]), .Q(A_q), .clk(and_1_out));  // open: en, clr
  Register #(.width(4)) B (.Q(B_q), .clk(and_1_out));  // open: D, en, clr
  Adder #(.width(4)) adder_1 (.a(A_q), .b(B_q), .out(adder_1_out), .cin(1'b0), .cout(adder_1_cout[8]));
  Register #(.width(4)) Q (.D(shifter_1_out[3:0]), .Q(Q_q), .clk(and_1_out));  // open: en, clr
  xor xor_1 (xor_1_out, Qs, Bs);
  Clock clock_1 (.out(clock_1_out));
  // Probe on xor_1_out
  Multiplexer #(.width(9), .enable("false")) multiplexer_1 (
    .in0({E_q[8], A_q, Q_q}), .in1({adder_1_cout[8], adder_1_out, Q_q}), .out(multiplexer_1_out), .sel(Q_q[0]));
  and and_1 (and_1_out, clock_1_out, not_1_out);
  Register #(.width(1)) E (.D(shifter_1_out[8]), .Q(E_q[8]), .clk(and_1_out));  // open: en, clr
  Shifter #(.width(9), .shift("lr")) shifter_1 (.in(multiplexer_1_out), .\dist (4'b0001), .out(shifter_1_out));
  Counter #(.width(3), .max('h4), .ongoal("stay")) SC (
    .carry(SC_carry), .clk(clock_1_out));  // open: load, D, count, Q, clr
  not not_1 (not_1_out, SC_carry);
endmodule
