// Logisim project PriorityEncoder.circ as structural Verilog: 1 circuit, main circuit main
module main (
  input  in_1,
  input  in_2,
  input  in_3,
  input  in_4,
  input  in_5,
  input  in_6,
  input  in_7,
  input  in_8
);

  wire and_1_out, and_2_out, and_3_out, and_4_out, and_5_out, and_6_out, controlled_buffer_1_out,
       controlled_buffer_2_out, controlled_buffer_3_out, or_1_out, or_2_out, or_3_out, or_4_out, or_5_out,
       or_6_out, or_7_out, or_8_out, or_9_out, or_10_out;

  or or_1 (or_1_out, or_2_out, in_4);
  or or_2 (or_2_out, or_3_out, in_5);
  or or_3 (or_3_out, or_4_out, in_6);
  or or_4 (or_4_out, in_8, in_7);
  or or_5 (or_5_out, or_6_out, in_1);
  or or_6 (or_6_out, or_7_out, in_2);
  or or_7 (or_7_out, or_1_out, in_3);
  and and_1 (and_1_out, in_2, ~or_7_out);  // AND_Gate
  and and_2 (and_2_out, in_3, ~or_1_out);  // AND_Gate
  and and_3 (and_3_out, in_4, ~or_2_out);  // AND_Gate
  and and_4 (and_4_out, in_5, ~or_3_out);  // AND_Gate
  and and_5 (and_5_out, in_6, ~or_4_out);  // AND_Gate
  and and_6 (and_6_out, in_7, ~in_8);  // AND_Gate
  or or_8 (or_8_out, and_1_out, and_3_out, and_5_out, in_8);
  or or_9 (or_9_out, and_2_out, and_3_out, and_6_out, in_8);
  or or_10 (or_10_out, and_4_out, and_5_out, and_6_out, in_8);
  // Probe on controlled_buffer_1_out
  assign controlled_buffer_1_out = or_5_out ? or_10_out : 1'bz;  // Controlled_Buffer controlled_buffer_1
  // Probe on controlled_buffer_2_out
  assign controlled_buffer_2_out = or_5_out ? or_9_out : 1'bz;  // Controlled_Buffer controlled_buffer_2
  // Probe on controlled_buffer_3_out
  assign controlled_buffer_3_out = or_5_out ? or_8_out : 1'bz;  // Controlled_Buffer controlled_buffer_3
endmodule
