// Logisim project Serial-Adder-Subtractor.circ as structural Verilog: 1 circuit, main circuit main
module main (
  input  in_1
);

  wire A_out, adder_1_cout, adder_1_out, and_1_out, and_2_out, and_3_out, B_out, clock_1_out, DFF_q,
       not_1_out, not_2_out, not_3_out, or_1_out, xor_1_out;
  wire [2:0] counter_1_q;

  Counter #(.width(3), .max('h7)) counter_1 (.Q(counter_1_q), .clk(clock_1_out));  // open: load, D, count, carry, clr
  Clock clock_1 (.out(clock_1_out));
  not not_1 (not_1_out, counter_1_q[0]);
  not not_2 (not_2_out, counter_1_q[1]);
  not not_3 (not_3_out, counter_1_q[2]);
  and and_1 (and_1_out, not_1_out, not_2_out, not_3_out);
  and and_2 (and_2_out, not_3_out, clock_1_out);
  Shift_Register #(.length(4)) A (
    .clk(and_2_out), .out(A_out));  // open: shift, in, load, clr, d0, q0, d1, q1, d2, q2, d3, q3
  Shift_Register #(.length(4)) B (
    .clk(and_2_out), .out(B_out));  // open: shift, in, load, clr, d0, q0, d1, q1, d2, q2, d3, q3
  xor xor_1 (xor_1_out, B_out, in_1);
  and and_3 (and_3_out, and_1_out, in_1);
  or or_1 (or_1_out, and_3_out, DFF_q);
  Adder #(.width(1)) adder_1 (.a(A_out), .b(xor_1_out), .out(adder_1_out), .cin(or_1_out), .cout(adder_1_cout));
  D_Flip_Flop DFF (.clk(and_2_out), .D(adder_1_cout), .Q(DFF_q));  // open: Qn, preset, en, reset
  Shift_Register #(.length(4)) S (
    .in(adder_1_out), .clk(and_2_out));  // open: shift, out, load, clr, d0, q0, d1, q1, d2, q2, d3, q3
endmodule
