// Logisim project Stack.circ as structural Verilog: 1 circuit, main circuit main
module main (
  input  [3:0] INPUT,
  input  _0_PUSH__1_POP,
  output [3:0] OUTPUT
);

  wire clock_1_out, not_1_out;
  wire [2:0] counter_1_q;

  Counter #(.width(3), .max('h7), .ongoal("stay")) counter_1 (
    .load(_0_PUSH__1_POP), .Q(counter_1_q), .clk(clock_1_out));  // open: D, count, carry, clr
  Clock clock_1 (.out(clock_1_out));
  not not_1 (not_1_out, _0_PUSH__1_POP);
  RAM #(.addrWidth(3), .dataWidth(4), .bus("separate")) ram_1 (
    .addr(counter_1_q), .din(INPUT), .data(OUTPUT), .str(not_1_out), .clk(clock_1_out), .ld(_0_PUSH__1_POP));  // open: sel, clr
endmodule
